# Fritzing sketch Temperature sensor on LCD (saved by Fritzing 0.9.4)
breadboards: 1

parts:
  Part1 = Arduino Uno (Rev3)
  LCD1 = LCD screen
  U1 = POT [package=pot_mammoth]
  T1 = LM35 Temperature Sensor [package="TO92 [THT]"]

nets:
  N1: Part1.A0, T1.Vout
  N2: Part1.D11_PWM/MOSI, LCD1.E
  N3: Part1.D12/MISO, LCD1.RS
  GND: Part1.GND, LCD1.VSS, LCD1.R/W, LCD1.LED-, U1.E, T1.GND
  N4: Part1.D2, LCD1.DB7
  N5: Part1.D3_PWM, LCD1.DB6
  N6: Part1.D4, LCD1.DB5
  N7: Part1.D5_PWM, LCD1.DB4
  5V: Part1.5V, LCD1.VDD, LCD1.LED+, U1.S, T1.+Vs
  N8: LCD1.V0, U1.A
